# Fritzing sketch Counter (saved by Fritzing 0.8.7b)
breadboards: 1

parts:
  7_Segment1 = 7 Segment Display
  Componente1 = Arduino Uno (Rev3)
  R1 = Resistor [tolerance=±5% resistance=220 package=THT]

nets:
  N1: 7_Segment1.Segment_E, Componente1.D6_PWM
  N2: 7_Segment1.Segment_D, Componente1.D5_PWM
  N3: 7_Segment1.common_anode, Componente1.GND, R1.Pin_0
  N4: 7_Segment1.Segment_C, Componente1.D4
  N5: 7_Segment1.Segment_DP, Componente1.D9_PWM
  N6: 7_Segment1.Segment_B, Componente1.D3_PWM
  N7: 7_Segment1.Segment_A, Componente1.D2
  N8: 7_Segment1.Segment_F, Componente1.D7
  N9: 7_Segment1.Segment_G, Componente1.D8
  N10: Componente1.3V3, R1.Pin_1
